# Fritzing sketch terrarium (saved by Fritzing 0.9.4)
breadboards: 1

parts:
  part = NodeMCU V1.0 [part_number=A]
  R1 = Resistor [tolerance=±5% resistance=10k package=THT]
  R2 = Resistor [tolerance=±5% resistance=10k package=THT]
  R3 = Resistor [tolerance=±5% resistance=4.7k package=THT]
  DS1 = DS18B20 1-Wire Temperature Sensor [part_number=DS18B20]  # not connected

nets:
  N1: part.D1, R1.Pin_0
  N2: part.D2, R2.Pin_0
  N3: part.3V3, R1.Pin_1, R2.Pin_1, R3.Pin_1
  N4: part.D5, R3.Pin_0

custom parts:
  NodeMCU V1.0: ESP8266 based NodeMCU

// code stored in the sketch: Node_B_receiver.ino
#include <SoftwareSerial.h>

#define D7 13
#define D8 15

SoftwareSerial mySerial(D7, D8); // RX = D7, TX  = D8


void setup() {
  Serial.begin(9600); //Start Serial
  mySerial.begin(9600); //Start mySerial
  pinMode(D7,INPUT); //d7 is RX, receiver, so define it as input
  pinMode(D8,OUTPUT); //d8 is TX, transmitter, so define it as output
} // end of setup

void loop() {
  char receivedLetter = '?'; // if empty show question mark
  
  if (mySerial.available() > 0) { //Check if serial is avaliable, if this check is not done you will read 'ÿ'
    receivedLetter = mySerial.read(); //read the char received. This function returns -1 if there is nothing to read.
    Serial.print("LETRA ");Serial.print(receivedLetter); Serial.println(" RECEBIDA"); // Write on serial monitor which letter was received. 
  }
  
} //end of loop
